// Digital circuit clock_with_enable.dig as structural Verilog
module clock_with_enable (
  input  ClkI,
  input  En,
  output ClkO
);

  wire and_1_out, counter_1_out, not_1_out;

  and and_1 (and_1_out, not_1_out, En);
  not not_1 (not_1_out, counter_1_out);
  Counter counter_1 (.en(and_1_out), .C(ClkI), .clr(1'b0), .out(counter_1_out));  // open: ovf
  and and_2 (ClkO, counter_1_out, ClkI);
endmodule
