// Digital circuit control_logic.dig as structural Verilog
module control_logic (
  input  Clk,
  input  [7:0] Inst,
  input  AEq,
  input  AGreater,
  input  AZero,
  output PCOut,
  output PCEnable,
  output PCClear,
  output PCLd,
  output ALUOut,
  output LdOut,
  output LdA,
  output EnA,
  output LdB,
  output EnB,
  output Sub,
  output LdInst,
  output EnInst,
  output LdMAddr,
  output MWr,
  output MEn,
  output Hlt,
  output LdFlags
);

  wire and_1_out, and_2_out, and_3_out, or_1_out;
  wire [1:0] rom_2_d;
  wire [2:0] counter_1_out, rom_1_d_2;
  wire [18:3] rom_1_d;

  or or_1 (or_1_out, AGreater, AEq);
  Counter #(.Bits(3)) counter_1 (.en(1'b1), .C(Clk), .clr(rom_1_d[18]), .out(counter_1_out));  // open: ovf
  ROM #(.AddrBits(8), .isProgramMemory("true"), .Bits(22)) rom_1 (
    .A({Inst[4:0], counter_1_out}), .sel(1'b1),
    .D({rom_1_d_2, rom_1_d[18], LdFlags, Hlt, MEn, MWr, LdMAddr, EnInst, LdInst, Sub, EnB, LdB, EnA, LdA, LdOut, ALUOut, rom_1_d[3], PCClear, PCEnable, PCOut}));
  and and_1 (and_1_out, rom_1_d[3], AEq);
  and and_2 (and_2_out, rom_1_d[3], or_1_out);
  and and_3 (and_3_out, rom_1_d[3], AZero);
  ROM #(.AddrBits(3), .Bits(2)) rom_2 (.A(rom_1_d_2), .sel(1'b1), .D(rom_2_d));
  Multiplexer #(.Selector_Bits(2)) multiplexer_1 (
    .sel(rom_2_d), .in_0(rom_1_d[3]), .in_1(and_1_out), .in_2(and_2_out), .in_3(and_3_out), .out(PCLd));

  // Notes on the sheet:
  //   // Ignore the 3 high bits, reserved for the microcode counter
  //   rom_1 loads rom.hex
  //   MPCRst
  //   PCLdIfEq
  //   PcLdIfGorEq
  //   PCLdIfZero
  //   If Equal
  //   If Greater or Equal
  //   If Zero
  //   contents of rom_2 (hex, n*v repeats v):
  //   0,1,2,0,3
endmodule
